# Fritzing sketch mini-piano (saved by Fritzing 0.9.3b)
circuit board: 8.46667cm x 5.64444cm
breadboards: 1

parts:
  Onderdeel2 = Arduino Uno (Rev3) - ICSP
  S1 = Momentary Switch [package=ksa_sealed_tac_switch]
  S3 = Pushbutton [package="[THT]"]
  S4 = Momentary Switch [package=ksa_sealed_tac_switch]
  S5 = Pushbutton [package="[THT]"]
  S6 = Pushbutton [package="[THT]"]
  J2 = Piezo Speaker
  R5 = Resistor [tolerance=±5% resistance=1k package="1206 [SMD]"]
  R6 = Resistor [tolerance=±5% resistance=1k package="1206 [SMD]"]
  R7 = Resistor [tolerance=±5% resistance=1k package="1206 [SMD]"]
  R8 = Resistor [tolerance=±5% resistance=1k package="1206 [SMD]"]
  R9 = Resistor [tolerance=±5% resistance=1k package="1206 [SMD]"]

nets:
  N1: Onderdeel2.D8, S6.Pin_3, S6.Pin_4
  N2: Onderdeel2.D11_PWM/MOSI, J2.pin13
  N3: Onderdeel2.D13/SCK, J2.pin11
  N4: Onderdeel2.GND, R5.Pin_1, R6.Pin_1, R7.Pin_1, R8.Pin_1, R9.Pin_1
  N5: Onderdeel2.D2, S4.3
  N6: Onderdeel2.D3_PWM, S1.3
  N7: Onderdeel2.D4, S3.Pin_3
  N8: Onderdeel2.D6_PWM, S5.Pin_3

custom parts:
  Piezo Speaker: Piezo
