# Fritzing sketch hc-05-relay out2 mobile control (saved by Fritzing 0.9.3b)

parts:
  LED17 = smd LED [color="Orange (620nm)" package="0603 [SMD]"]
  LED19 = smd LED [color="Blue (430nm)" package="0603 [SMD]"]  # not connected
  LED21 = smd LED [color="Green (555nm)" package="0603 [SMD]"]
  LED22 = smd LED [color="Yellow (595nm)" package="0603 [SMD]"]
  LED24 = smd LED [color="Red (633nm)" package="0603 [SMD]"]
  JY-MCU1 = Arduino Nano (Rev3.0)
  R17 = Resistor [tolerance=±5% resistance=220 package=THT]
  R18 = Resistor [tolerance=±5% resistance=220 package=THT]
  R19 = Resistor [tolerance=±5% resistance=220 package=THT]
  R20 = Resistor [tolerance=±5% resistance=220 package=THT]
  R21 = Resistor [tolerance=±5% resistance=220 package=THT]
  Power_plug4 = Power plug
  R22 = Resistor [tolerance=±5% resistance=2.2k package=THT]
  R24 = Resistor [tolerance=±5% resistance=1k package=THT]
  Part4 = Lilypad Battery Connect
  U4 = SWITCH-SPST-2 [package=switch-spst-vertical]
  Part5 = Lilypad Battery Connect
  Z1 = VARISTOR [package=0603-res]
  LED29 = smd LED [color="Orange (620nm)" package="0603 [SMD]"]  # not connected
  U3 = 4-Channel 5v Relay Shield [package=relay-4ch5v10a]
  R25 = Resistor [tolerance=±5% resistance=220 package=THT]
  LED27 = LEDs [package=led10mm]
  Part3 = Bluetooth HC-05 Macho
  LED3 = LEDs [package=led10mm]

nets:
  N1: LED17.cathode, LED21.cathode, LED22.cathode, LED24.cathode
  N2: JY-MCU1.D2, Part3.TXD
  N3: JY-MCU1.D3, R24.Pin_0
  N4: JY-MCU1.D4, R20.Pin_1
  N5: JY-MCU1.D5, R18.Pin_1
  N6: JY-MCU1.D6, R21.Pin_1
  N7: JY-MCU1.D7, R19.Pin_1
  N8: JY-MCU1.D8, R17.Pin_1
  N9: JY-MCU1.D9, U3.IN4
  N10: JY-MCU1.D10, U3.IN3
  N11: JY-MCU1.D12/MISO, U3.IN1
  N12: JY-MCU1.VIN, U4.P
  GND: JY-MCU1.GND, JY-MCU1.RESET, R22.Pin_0, U3.GND, Part3.GND
  VCC: JY-MCU1.5V, U3.VCC, Part3.VCC
  N13: JY-MCU1.D13/SCK, R25.Pin_1
  N14: Power_plug4.VCC, U4.O
  N15: R22.Pin_1, Part3.RXD
  N16: Part4.-, U3.K3-Off, U3.K4-On
  N17: Part4.+, U3.K4-In
  N18: Part5.-, U3.K1-Off, U3.K2-On
  N19: Part5.+, U3.K2-In
  N20: Z1.1, Z1.2
  N21: U3.K1-In, LED27.A
  N22: U3.K3-In, LED3.A

notes:
  220V AC power supply
  input
  5-12 DC IN
  S2
  Hand held Switch
  10A
  220 AC
  relay1
  relay2
  relay3
  relay4
  VCC
  D9
  D10
  D11
  D12
  GND
  ON / OFF
  Arduino
  S1
  Hand held Switch
  Load2
  Load1
  D8 D7 D6 D5 D4 D13
  D8=Load1
  D7=Load2
  D6=All control
  D5=Mode 0
  handheld mode
  D4=Mode 1
  mobile mode
  D13=No opration
  other switch mobile App
  D9&D11=Switch ON/OFF Load1,2
  D12&D10=Mode Changing

custom parts:
  4-Channel 5v Relay Shield: 4 Channel 5v Relay Shield w. 2x SPD-06VDC-SD-C
