# Fritzing sketch esp32rfid (saved by Fritzing 0.9.3b)
breadboards: 2

parts:
  U1 = ESP32S-HiLetgo [part_number=ESP32S-HiLetgo]
  IC1 = 25LC512 [package=THT]
  U2 = 2.4" TFT LCD screen, SPI, Touch-enabled
  RFID1 = RFID Reader
  U3 = RELAY-SOLIDSTATE [package=relay-s108t02]
  Part1 = KY-021 Mini Magnetic Reed Switch Module [package="Breakout board"]

nets:
  GND: U1.GND, IC1.0V, U2.GND, RFID1.GND, RFID1.+/-, U3.-, Part1.-
  VIN: U1.VIN, RFID1.RES, RFID1.+5V
  N1: U1.GPIO2, IC1.CS_-_Chip_Select
  N2: U1.GPIO0, U2.DC
  N3: U1.GPIO4, U2.CS
  N4: U1.GPIO16, RFID1.D1
  N5: U1.GPIO5, U2.RESET
  N6: U1.GPIO18, IC1.SI_-_Data_In, U2.SCL
  N7: U1.GPIO19, IC1.SO_-_Data_Out
  N8: U1.GPIO23, IC1.SCK_-_SPI_Clock, U2.SDA
  VCC: IC1.WP_-_Write_Protect, IC1.HOLD, IC1.+V, U2.LED, U2.VCC, Part1.Vin

custom parts:
  ESP32S-HiLetgo: HiLetgo ESP-WROOM-32 ESP32 ESP-32S Development Board 2.4GHz Dual-Mode WiFi + Bluetooth Dual Cores Microcontroller The ESP32 integrated with Antenna switches, RF Balun, power amplifiers, low-noise amplifiers, filters, and management modules, and the entire solution occupies the least area of PCB. 2.4 GHz Wi-Fi plus Bluetooth dual-mode chip, with TSMC Ultra-low power consumption 40nm technology,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
  2.4" TFT LCD screen, SPI, Touch-enabled: 2.4", ILI9341-based TFT LCD screen with touch-sensing using the XPT2046 controller, SPI-compatible. There is also an SD-card version that is non-touch enabled but uses exactly the same board and pinout. This part is for both, though it should be noted that the SD reader and the touch screen are mutually incompatible
  KY-021 Mini Magnetic Reed Switch Module: KY-021 magnetic reed switch module. A reed switch is a magnetic sensor that is normally open and gets closed when exposed to a magnetic field.
