# Fritzing sketch rfid-rc522 (saved by Fritzing 0.9.3b)
breadboards: 1

parts:
  Part2 = Arduino Uno (Rev3) - ICSP
  ZS-042_RTC1 = ZS-042 RTC Module
  MicroSD_card_adapter = MicroSD Card Module
  Part1 = RFID-RC522-v2
  LED1 = LED - 5mm [color="Red (633nm)" package="5 mm [THT]"]
  LED2 = LED - 5mm [color="Green (555nm)" package="5 mm [THT]"]
  J1 = Piezo Speaker
  R1 = Resistor [tolerance=±5% resistance=220 package=THT]
  R2 = Resistor [tolerance=±5% resistance=220 package=THT]

nets:
  N1: Part2.D9_PWM, Part1.RST
  N2: Part2.D10_PWM/SS, Part1.SDA
  N3: Part2.D11_PWM/MOSI, MicroSD_card_adapter.MOSI, Part1.MOSI
  N4: Part2.D12/MISO, MicroSD_card_adapter.MISO, Part1.MISO
  N5: Part2.D13/SCK, MicroSD_card_adapter.SCK, Part1.SCK
  N6: Part2.A4/SDA, ZS-042_RTC1.SDA
  N7: Part2.A5/SCL, ZS-042_RTC1.SCL
  N8: Part2.D4, MicroSD_card_adapter.CS
  N9: Part2.D5_PWM, J1.pin2
  N10: Part2.D6_PWM, LED1.cathode
  N11: Part2.D7, LED2.cathode
  3V3: Part2.3V3, Part1.3.3V
  VCC: Part2.5V, ZS-042_RTC1.VCC, MicroSD_card_adapter.VCC
  GND: Part2.GND, ZS-042_RTC1.GND, MicroSD_card_adapter.GND, Part1.GND, J1.pin1, R1.Pin_0, R2.Pin_0
  N12: LED1.anode, R2.Pin_1
  N13: LED2.anode, R1.Pin_1

notes:
  DS3231 RTC module

custom parts:
  ZS-042 RTC Module: This is the ZS-042 RTC module which uses the Maxim DS3231 real time clock IC. The module has a battery holder for a LIR2032 or CR2032. The module also includes an Atmel AT24C32 32K EEPROM for storing important information. The module can operate at 3V3 and 5V.
  RFID-RC522-v2: A simple China made RFID-RC522 Reader; do check the pin labels, as this is a MFRC522 based clone.

// code stored in the sketch: Untitled2.ino
#include <MFRC522.h> // for the RFID
#include <SPI.h> // for the RFID and SD card module
#include <SD.h> // for the SD card
#include <RTClib.h> // for the RTC

// define pins for RFID
#define CS_RFID 10
#define RST_RFID 9
// define select pin for SD card module
#define CS_SD 4 

// Create a file to store the data
File myFile;

// Instance of the class for RFID
MFRC522 rfid(CS_RFID, RST_RFID); 

// Variable to hold the tag's UID
String uidString;

// Instance of the class for RTC
RTC_DS1307 rtc;

// Define check in time
const int checkInHour = 9;
const int checkInMinute = 5;

//Variable to hold user check in
int userCheckInHour;
int userCheckInMinute;

// Pins for LEDs and buzzer
const int redLED = 6;
const int greenLED = 7;
const int buzzer = 5;

void setup() {
  
  // Set LEDs and buzzer as outputs
  pinMode(redLED, OUTPUT);  
  pinMode(greenLED, OUTPUT);
  pinMode(buzzer, OUTPUT);
  
  // Init Serial port
  Serial.begin(9600);
  while(!Serial); // for Leonardo/Micro/Zero
  
  // Init SPI bus
  SPI.begin(); 
  // Init MFRC522 
  rfid.PCD_Init(); 

  // Setup for the SD card
  Serial.print("Initializing SD card...");
  if(!SD.begin(CS_SD)) {
    Serial.println("initialization failed!");
    return;
  }
  Serial.println("initialization done.");

  // Setup for the RTC  
  if(!rtc.begin()) {
    Serial.println("Couldn't find RTC");
    while(1);
  }
  else {
    // following line sets the RTC to the date & time this sketch was compiled
    rtc.adjust(DateTime(F(__DATE__), F(__TIME__)));
  }
  if(!rtc.isrunning()) {
    Serial.println("RTC is NOT running!");
  }
}

void loop() {
  //look for new cards
  if(rfid.PICC_IsNewCardPresent()) {
    readRFID();
    logCard();
    verifyCheckIn();
  }
  delay(10);
}

void readRFID() {
  rfid.PICC_ReadCardSerial();
  Serial.print("Tag UID: ");
  uidString = String(rfid.uid.uidByte[0]) + " " + String(rfid.uid.uidByte[1]) + " " + 
    String(rfid.uid.uidByte[2]) + " " + String(rfid.uid.uidByte[3]);
  Serial.println(uidString);
 
  // Sound the buzzer when a card is read
  tone(buzzer, 2000); 
  delay(100);        
  noTone(buzzer);
  
  delay(100);
}

void logCard() {
  // Enables SD card chip select pin
  digitalWrite(CS_SD,LOW);
  
  // Open file
  myFile=SD.open("DATA.txt", FILE_WRITE);

  // If the file opened ok, write to it
  if (myFile) {
    Serial.println("File opened ok");
    myFile.print(uidString);
    myFile.print(", ");   
    
    // Save time on SD card
    DateTime now = rtc.now();
    myFile.print(now.year(), DEC);
    myFile.print('/');
    myFile.print(now.month(), DEC);
    myFile.print('/');
    myFile.print(now.day(), DEC);
    myFile.print(',');
    myFile.print(now.hour(), DEC);
    myFile.print(':');
    myFile.println(now.minute(), DEC);
    
    // Print time on Serial monitor
    Serial.print(now.year(), DEC);
    Serial.print('/');
    Serial.print(now.month(), DEC);
    Serial.print('/');
    Serial.print(now.day(), DEC);
    Serial.print(' ');
    Serial.print(now.hour(), DEC);
    Serial.print(':');
    Serial.println(now.minute(), DEC);
    Serial.println("sucessfully written on SD card");
    myFile.close();

    // Save check in time;
    userCheckInHour = now.hour();
    userCheckInMinute = now.minute();
  }
  else {
    Serial.println("error opening data.txt");  
  }
  // Disables SD card chip select pin  
  digitalWrite(CS_SD,HIGH);
}

void verifyCheckIn(){
  if((userCheckInHour < checkInHour)||((userCheckInHour==checkInHour) && (userCheckInMinute <= checkInMinute))){
    digitalWrite(greenLED, HIGH);
    delay(2000);
    digitalWrite(greenLED,LOW);
    Serial.println("You're welcome!");
  }
  else{
    digitalWrite(redLED, HIGH);
    delay(2000);
    digitalWrite(redLED,LOW);
    Serial.println("You are late...");
  }
}

